// Logisim project lab1.circ as structural Verilog: 3 circuits, main circuit main
module main (
  input  A,
  input  B,
  output S
);

  wire and_1_out, and_2_out;

  and and_1 (and_1_out, ~A, B);  // AND_Gate
  and and_2 (and_2_out, A, ~B);  // AND_Gate
  or or_1 (S, and_1_out, and_2_out);
endmodule

module add1 (
  input  A,
  input  B,
  input  Cin,
  output S,
  output Cout
);

  wire and_1_out, and_2_out, xor_1_out;

  xor xor_1 (xor_1_out, A, B);
  xor xor_2 (S, xor_1_out, Cin);
  and and_1 (and_1_out, xor_1_out, Cin);
  and and_2 (and_2_out, A, B);
  or or_1 (Cout, and_1_out, and_2_out);
endmodule

module four_bit_adder (
  input  [3:0] A,
  input  [3:0] B,
  input  Cin,
  output Cout,
  output [3:0] S
);

  wire add1_1_cout, add1_2_cout, add1_3_cout;

  add1 add1_1 (.A(A[0]), .B(B[0]), .Cin(Cin), .S(S[0]), .Cout(add1_1_cout));
  add1 add1_2 (.A(A[1]), .B(B[1]), .Cin(add1_1_cout), .S(S[1]), .Cout(add1_2_cout));
  add1 add1_3 (.A(A[2]), .B(B[2]), .Cin(add1_2_cout), .S(S[2]), .Cout(add1_3_cout));
  add1 add1_4 (.A(A[3]), .B(B[3]), .Cin(add1_3_cout), .S(S[3]), .Cout(Cout));
endmodule
