// Logisim project leftshift32_template.circ as structural Verilog: 6 circuits, main circuit LeftShift32
module LeftShift32 (
  input  [31:0] B,
  input  [4:0] Sa,
  input  Cin,
  output [31:0] C
);

  wire [31:0] leftshift1_1_c, leftshift2_1_c, leftshift4_1_c, leftshift8_1_c, leftshift16_1_c,
       multiplexer_1_out, multiplexer_2_out, multiplexer_3_out, multiplexer_4_out;

  LeftShift16 leftshift16_1 (.Cin(Cin), .B(B), .C(leftshift16_1_c));
  Multiplexer #(.width(32)) multiplexer_1 (.in0(B), .in1(leftshift16_1_c), .out(multiplexer_1_out), .sel(Sa[4]));
  LeftShift8 leftshift8_1 (.Cin(Cin), .B(multiplexer_1_out), .C(leftshift8_1_c));
  Multiplexer #(.width(32)) multiplexer_2 (
    .in0(multiplexer_1_out), .in1(leftshift8_1_c), .out(multiplexer_2_out), .sel(Sa[3]));
  LeftShift4 leftshift4_1 (.Cin(Cin), .B(multiplexer_2_out), .C(leftshift4_1_c));
  Multiplexer #(.width(32)) multiplexer_3 (
    .in0(multiplexer_2_out), .in1(leftshift4_1_c), .out(multiplexer_3_out), .sel(Sa[2]));
  LeftShift2 leftshift2_1 (.Cin(Cin), .B(multiplexer_3_out), .C(leftshift2_1_c));
  Multiplexer #(.width(32)) multiplexer_4 (
    .in0(multiplexer_3_out), .in1(leftshift2_1_c), .out(multiplexer_4_out), .sel(Sa[1]));
  LeftShift1 leftshift1_1 (.Cin(Cin), .B(multiplexer_4_out), .C(leftshift1_1_c));
  Multiplexer #(.width(32)) multiplexer_5 (.in0(multiplexer_4_out), .in1(leftshift1_1_c), .out(C), .sel(Sa[0]));
endmodule

module LeftShift1 (
  input  Cin,
  input  [31:0] B,
  output [31:0] C
);


  assign C = {B[30:0], Cin};
endmodule

module LeftShift2 (
  input  Cin,
  input  [31:0] B,
  output [31:0] C
);

  wire [31:0] leftshift1_1_c;

  LeftShift1 leftshift1_1 (.Cin(Cin), .B(B), .C(leftshift1_1_c));
  LeftShift1 leftshift1_2 (.Cin(Cin), .B(leftshift1_1_c), .C(C));
endmodule

module LeftShift4 (
  input  Cin,
  input  [31:0] B,
  output [31:0] C
);

  wire [31:0] leftshift2_1_c;

  LeftShift2 leftshift2_1 (.Cin(Cin), .B(B), .C(leftshift2_1_c));
  LeftShift2 leftshift2_2 (.Cin(Cin), .B(leftshift2_1_c), .C(C));
endmodule

module LeftShift8 (
  input  Cin,
  input  [31:0] B,
  output [31:0] C
);

  wire [31:0] leftshift4_1_c;

  LeftShift4 leftshift4_1 (.Cin(Cin), .B(B), .C(leftshift4_1_c));
  LeftShift4 leftshift4_2 (.Cin(Cin), .B(leftshift4_1_c), .C(C));
endmodule

module LeftShift16 (
  input  Cin,
  input  [31:0] B,
  output [31:0] C
);

  wire [31:0] leftshift8_1_c;

  LeftShift8 leftshift8_1 (.Cin(Cin), .B(B), .C(leftshift8_1_c));
  LeftShift8 leftshift8_2 (.Cin(Cin), .B(leftshift8_1_c), .C(C));
endmodule
